// Logisim project cpu.circ as structural Verilog: 1 circuit, main circuit cpu
module cpu (
  input  clk,
  input  [31:0] INSTRUCTION,
  input  [31:0] READ_DATA,
  output [31:0] WRITE_ADDRESS,
  output [31:0] PROGRAM_COUNTER,
  output [31:0] ra,
  output [31:0] sp,
  output [31:0] t0,
  output [31:0] t1,
  output [31:0] t2,
  output [31:0] s0,
  output [31:0] s1,
  output [31:0] a0,
  output [31:0] tohost,
  output [3:0] WRITE_ENABLE,
  output [31:0] WRITE_DATA
);

  wire alu_1_p5, alu_1_p6, ASel, BrEq, BrLt, BrUn, BSel, CSRSel, CSRWen, MemRW, PCSel, regfile_1_p7,
       regfile_1_p8, regfile_1_p10, regfile_1_p22, regfile_1_p24, regfile_1_p26, RegWEn;
  wire [1:0] WBSel;
  wire [2:0] funct3, ImmSel;
  wire [3:0] ALUSel;
  wire [6:0] funct7;
  wire [24:0] INST_ID;
  wire [31:0] adder_1_out, adder_2_out, imm, multiplexer_1_out, multiplexer_2_out, multiplexer_3_out,
       multiplexer_4_out, multiplexer_5_out, PC_ID, read_data1, WB_DATA;

  Adder #(.width(32)) adder_1 (.a(PROGRAM_COUNTER), .b(32'h4), .out(adder_1_out));  // open: cin, cout
  Multiplexer #(.enable("false"), .width(32)) multiplexer_1 (
    .in0(adder_1_out), .in1(WRITE_ADDRESS), .out(multiplexer_1_out), .sel(PCSel));
  Register #(.width(32)) PC (.D(multiplexer_1_out), .clk(clk), .Q(PROGRAM_COUNTER));  // open: en, clr
  Multiplexer #(.enable("false"), .width(32)) multiplexer_2 (
    .in0(INSTRUCTION), .in1(32'h13), .out(multiplexer_2_out), .sel(PCSel));
  control_logic control_logic_1 (
    .CSRWen(CSRWen), .PCSel(PCSel), .RegWEn(RegWEn), .ImmSel(ImmSel), .BrUn(BrUn), .ASel(ASel), .BSel(BSel),
    .ALUSel(ALUSel), .MemRW(MemRW), .WBSel(WBSel), .CSRSel(CSRSel),
    .inst({funct7, INST_ID[24:15], funct3, INST_ID[11:0]}), .BrEq(BrEq), .BrLt(BrLt));
  Register #(.width(32)) Inst_Pipelined (
    .D(multiplexer_2_out), .clk(clk), .Q({funct7, INST_ID[24:15], funct3, INST_ID[11:0]}));  // open: en, clr
  Register #(.width(32)) PC_Pipelined (.D(PROGRAM_COUNTER), .clk(clk), .Q(PC_ID));  // open: en, clr
  // regfile regfile_1: pin names not known; wires that end beside it: INST_ID[19:15], INST_ID[24:20], INST_ID[11:7], WB_DATA, RegWEn, clk, regfile_1_p7, regfile_1_p8, regfile_1_p8, regfile_1_p10, regfile_1_p10, ra, sp, t0, t1, t2, s0, s1, a0, read_data1, WRITE_DATA, regfile_1_p22, regfile_1_p22, regfile_1_p24, regfile_1_p24, regfile_1_p26, regfile_1_p26
  imm_gen imm_gen_1 (.inst({funct7, INST_ID[24:15], funct3, INST_ID[11:0]}), .ImmSel(ImmSel), .imm(imm));
  Multiplexer #(.enable("false"), .width(32)) multiplexer_3 (
    .in0(read_data1), .in1(PC_ID), .out(multiplexer_3_out), .sel(ASel));
  Multiplexer #(.enable("false"), .width(32)) multiplexer_4 (
    .in0(WRITE_DATA), .in1(imm), .out(multiplexer_4_out), .sel(BSel));
  // alu alu_1: pin names not known; wires that end beside it: multiplexer_3_out, multiplexer_4_out, ALUSel, WRITE_ADDRESS, alu_1_p5, alu_1_p6
  branch_comp branch_comp_1 (.rs1(read_data1), .rs2(WRITE_DATA), .BrUn(BrUn), .BrEq(BrEq), .BrLt(BrLt));
  Multiplexer #(.enable("false"), .width(32)) multiplexer_5 (
    .in0(read_data1), .in1(imm), .out(multiplexer_5_out), .sel(CSRSel));
  assign WRITE_ENABLE = {{3{MemRW}}, MemRW};  // Bit_Extender bit_extender_1
  csr csr_1 (.CSR_address(12'h51e), .CSR_din(multiplexer_5_out), .CSR_WE(CSRWen), .clk(clk), .tohost(tohost));
  Adder #(.width(32)) adder_2 (.a(PC_ID), .b(32'h4), .out(adder_2_out));  // open: cin, cout
  Multiplexer #(.enable("false"), .select(2), .width(32)) multiplexer_6 (
    .in0(READ_DATA), .in1(WRITE_ADDRESS), .in2(adder_2_out), .out(WB_DATA), .sel(WBSel));  // open: in3

  // Other names for the same wires on the sheet: alu_output[31:0] = WRITE_ADDRESS; opcode[6:0] = INST_ID[6:0];
  //   rd[4:0] = INST_ID[11:7]; INST_ID (some bits) = {funct7, funct3}; rs1[4:0] = INST_ID[19:15];
  //   rs2[4:0] = INST_ID[24:20]; read_data2[31:0] = WRITE_DATA

  // Notes on the sheet:
  //   Output to IMEM
  //   IMEM (do **NOT** move this)
  //   Inputs from IMEM
  //   It is OK to move the PC, RegFile, ALU, MEM, Branch Comp, Imm Gen, and Control Logic to wherever is most convenient for you when constructing your CPU, and to delete this text
  //   Inputs/Outputs for testing. Do **NOT** move these.
  //   Outputs To DMEM
  //   DMEM (do **NOT** move this)
  //   Inputs From DMEM
endmodule
