// Logisim project imm_gen.circ as structural Verilog: 1 circuit, main circuit imm_gen
module imm_gen (
  input  [31:0] inst,
  input  [2:0] ImmSel,
  output [31:0] imm
);

  wire [11:11] S_IMM;
  wire [31:0] CSRRW_IMM, I_IMM, J_IMM;
  wire [31:1] B_IMM;

  Multiplexer #(.enable("false"), .select(3), .width(32)) multiplexer_1 (
    .in0(I_IMM), .in1({B_IMM[31:12], S_IMM[11], B_IMM[10:1], B_IMM[11]}), .in2({B_IMM, 1'b0}),
    .in3({inst[31:12], {12{1'b0}}}), .in4(J_IMM), .in5(CSRRW_IMM), .out(imm), .sel(ImmSel));  // open: in6, in7
  assign CSRRW_IMM = {{27{1'b0}}, inst[19:15]};  // Bit_Extender bit_extender_1
  assign I_IMM = {{20{inst[31]}}, inst[31:20]};  // Bit_Extender bit_extender_2
  assign {B_IMM[31:12], S_IMM[11], B_IMM[10:1], B_IMM[11]} = {{20{inst[31]}}, {inst[31:25], inst[11:7]}};  // Bit_Extender bit_extender_3
  assign J_IMM = {{11{inst[31]}}, {inst[31], inst[19:12], inst[20], inst[30:21], 1'b0}};  // Bit_Extender bit_extender_4

  // Other names for the same wires on the sheet: S_IMM (some bits) = {B_IMM[31:12], B_IMM[10:1], B_IMM[11]};
  //   opcode[6:0] = inst[6:0]; rd[4:0] = inst[11:7]; s_imm_t[11:0] = {inst[31:25], inst[11:7]};
  //   funct3[2:0] = inst[14:12]; j_imm_t[20:1] = {inst[31], inst[19:12], inst[20], inst[30:21]};
  //   U_IMM[31:12] = inst[31:12]; rs1[4:0] = inst[19:15]; i_imm_t[11:0] = inst[31:20]; rs2[4:0] = inst[24:20];
  //   funct7[6:0] = inst[31:25]

  // Notes on the sheet:
  //   INPUTS to your circuit
  //   DON'T CHANGE THE LOCATIONS OF THE INPUTS AND OUTPUTS!
  //   OUTPUT from your circuit
endmodule
